# Fritzing sketch schematic (saved by Fritzing 0.9.3b)

parts:
  M1 = Wemos ESP-Wroom-02 [package=THT]
  Part1 = DHT22 module
  OLED1 = OLED 128x64 I2C Monochrome Display

nets:
  N1: M1.pin2, OLED1.SCK
  N2: M1.pin3, OLED1.SDA
  N3: M1.pin5, Part1.DATA
  VCC: M1.pin12, M1.pin13, Part1.VCC, OLED1.VDD
  GND: M1.pin15, M1.pin16, Part1.GND, OLED1.GND

custom parts:
  Wemos ESP-Wroom-02: Wemos ESP-Wroom-02 with 18650 battery on the back. Due the battery on the bottom, breadboard view and PCB view are backwards from normal (i.e.) they assume you will be mounting the module with the battery facing up rather than the usual orientation).
